# Fritzing sketch wiring (saved by Fritzing 0.9.0b)
breadboards: 1

parts:
  Part1 = MD10C R2
  Part2 = Arduino Uno (Rev3)  # not connected
  VCC1 = Battery
  M1 = DC Motor

nets:
  N1: Part1.no_name_yet#connectorA-3, M1.pin_2
  N2: Part1.no_name_yet#connectorB-4, M1.pin_1
  N3: Part1.no_name_yet#connector_3, Part1.no_name_yet#connectornegative-2, VCC1.-
  N4: Part1.no_name_yet#connectorpositive-1, VCC1.+
